# Fritzing sketch wirings (saved by Fritzing 0.9.2b)
breadboards: 1

parts:
  Part1 = RFID-RC522-v2
  U1 = NodeMCU V1.0
  LED1 = RGB LED (com. cathode, rgb) [package="5 mm [THT]"]
  Q3 = TRANSISTOR_NPN [package=to-92-ammo]
  R1 = Resistor [tolerance=±5% resistance=1k package="0402 [SMD]"]
  R2 = Resistor [tolerance=±5% resistance=1k package="0402 [SMD]"]
  R3 = Resistor [tolerance=±5% resistance=1k package="0402 [SMD]"]
  X1 = USB Connectors [package=usb-a-s-silk-female]
  R4 = Resistor [tolerance=±5% resistance=220 package="0402 [SMD]"]
  R5 = Resistor [tolerance=±5% resistance=220 package="0402 [SMD]"]
  R6 = Resistor [tolerance=±5% resistance=220 package="0402 [SMD]"]
  Q1 = TRANSISTOR_NPN [package=to-92-ammo]
  Q2 = TRANSISTOR_NPN [package=to-92-ammo]

nets:
  N1: Part1.SDA, U1.D0
  N2: Part1.SCK, U1.D5
  N3: Part1.MOSI, U1.D7
  N4: Part1.MISO, U1.D6
  GND: Part1.GND, U1.GND, LED1.common_cathode, X1.GND
  N5: Part1.RST, U1.D1
  3.3V: Part1.3.3V, U1.3V3
  N6: U1.D2, R1.Pin_0
  N7: U1.D3, R2.Pin_0
  N8: U1.D8, R3.Pin_0
  N9: LED1.red_anode, Q2.E
  N10: LED1.green_anode, Q3.E
  N11: LED1.blue_anode, Q1.E
  N12: Q3.B, R3.Pin_1
  N13: Q3.C, R4.Pin_1
  N14: R1.Pin_1, Q1.B
  N15: R2.Pin_1, Q2.B
  N16: X1.VBUS, R4.Pin_0, R5.Pin_0, R6.Pin_0
  N17: R5.Pin_1, Q2.C
  N18: R6.Pin_1, Q1.C

notes:
  see pinout
  http://www.cnx-software.com/wp-content/uploads/2015/04/NodeMCU_Pinout.png
  when programming use gpio numbers (not the nodmcu numbers)

custom parts:
  RFID-RC522-v2: A simple China made RFID-RC522 Reader; do check the pin labels, as this is a MFRC522 based clone.
  NodeMCU V1.0: ESP9266 based NodeMCU
